// Logisim project cpu.circ as structural Verilog: 8 circuits, main circuit main
module main (
);

  wire ALC, ALO, ALS, and_1_out, clock_1_out, FE, HLT, IE, IRE, IRO, JMP, MAE, not_1_out, not_2_out, PCE,
       PCO, RAE, RAO, XE, XO, YE, YO, ZE, ZO;
  wire [2:0] InstructionStepCounter_q;
  wire [7:0] controlled_buffer_4_out, FlagsReg_q;
  wire [7:3] InstructionRegister_q_2;
  wire [10:0] controlled_buffer_1_out, controlled_buffer_13_out, InstructionRegister_q,
       MemoryAddressRegister_q, ProgramCounter_q;
  wire [15:0] alu_1_aluout, controlled_buffer_2_out, controlled_buffer_5_out, controlled_buffer_7_out,
       controlled_buffer_9_out, controlled_buffer_11_out, controlled_buffer_14_out, ram_1_dout, XReg_q,
       YReg_q, ZReg_q;
  wire [15:11] controlled_buffer_12_out;

  Counter #(.max('h7), .width(3)) InstructionStepCounter (
    .load(IE), .up(1'b1), .count(1'b1), .clk(not_1_out), .D(3'b000), .Q(InstructionStepCounter_q));  // open: clr, carry
  not not_1 (not_1_out, and_1_out);
  ROM #(.addrWidth(11), .dataWidth(20)) rom_1 (
    .addr({FlagsReg_q[2:0], InstructionRegister_q_2, InstructionStepCounter_q}),
    .data({HLT, PCE, PCO, JMP, XE, XO, YE, YO, ZE, ZO, IRE, IRO, MAE, RAE, RAO, FE, ALO, ALS, ALC, IE}));
  Clock clock_1 (.out(clock_1_out));
  not not_2 (not_2_out, HLT);
  assign controlled_buffer_1_out = JMP ? controlled_buffer_2_out[10:0] : 11'bz;  // Controlled_Buffer controlled_buffer_1
  and and_1 (and_1_out, clock_1_out, not_2_out);
  Counter #(.max('h7ff), .width(11)) ProgramCounter (
    .load(JMP), .up(1'b1), .count(PCE), .clk(and_1_out), .D(controlled_buffer_1_out), .Q(ProgramCounter_q));  // open: clr, carry
  LED led_1 (.in(controlled_buffer_2_out[15]));
  ALU alu_1 (.XReg(XReg_q), .YReg(YReg_q), .ALS(ALS), .ALC(ALC), .ALUOut(alu_1_aluout));  // open: CFOut
  LED led_2 (.in(controlled_buffer_2_out[14]));
  LED led_3 (.in(controlled_buffer_2_out[13]));
  LED led_4 (.in(controlled_buffer_2_out[12]));
  LED led_5 (.in(controlled_buffer_2_out[11]));
  assign controlled_buffer_2_out[10:0] = PCO ? ProgramCounter_q : 11'bz;  // Controlled_Buffer controlled_buffer_2
  assign controlled_buffer_2_out = ALO ? alu_1_aluout : 16'bz;  // Controlled_Buffer controlled_buffer_3
  Pull_Resistor pull_resistor_1 (.node(controlled_buffer_2_out[15]));
  Pull_Resistor pull_resistor_2 (.node(controlled_buffer_2_out[14]));
  Pull_Resistor pull_resistor_3 (.node(controlled_buffer_2_out[13]));
  Pull_Resistor pull_resistor_4 (.node(controlled_buffer_2_out[12]));
  LED led_6 (.in(controlled_buffer_2_out[10]));
  LED led_7 (.in(controlled_buffer_2_out[9]));
  LED led_8 (.in(controlled_buffer_2_out[8]));
  Pull_Resistor pull_resistor_5 (.node(controlled_buffer_2_out[11]));
  Pull_Resistor pull_resistor_6 (.node(controlled_buffer_2_out[10]));
  LED led_9 (.in(controlled_buffer_2_out[7]));
  LED led_10 (.in(controlled_buffer_2_out[6]));
  LED led_11 (.in(controlled_buffer_2_out[5]));
  LED led_12 (.in(controlled_buffer_2_out[4]));
  Pull_Resistor pull_resistor_7 (.node(controlled_buffer_2_out[9]));
  Pull_Resistor pull_resistor_8 (.node(controlled_buffer_2_out[8]));
  Pull_Resistor pull_resistor_9 (.node(controlled_buffer_2_out[7]));
  Pull_Resistor pull_resistor_10 (.node(controlled_buffer_2_out[6]));
  Pull_Resistor pull_resistor_11 (.node(controlled_buffer_2_out[5]));
  Pull_Resistor pull_resistor_12 (.node(controlled_buffer_2_out[4]));
  Pull_Resistor pull_resistor_13 (.node(controlled_buffer_2_out[3]));
  Pull_Resistor pull_resistor_14 (.node(controlled_buffer_2_out[2]));
  LED led_13 (.in(controlled_buffer_2_out[3]));
  LED led_14 (.in(controlled_buffer_2_out[2]));
  LED led_15 (.in(controlled_buffer_2_out[1]));
  LED led_16 (.in(controlled_buffer_2_out[0]));
  assign controlled_buffer_4_out = FE ? {8{1'b0}} : 8'bz;  // Controlled_Buffer controlled_buffer_4
  assign controlled_buffer_5_out = XE ? controlled_buffer_2_out : 16'bz;  // Controlled_Buffer controlled_buffer_5
  assign controlled_buffer_2_out = XO ? XReg_q : 16'bz;  // Controlled_Buffer controlled_buffer_6
  assign controlled_buffer_7_out = YE ? controlled_buffer_2_out : 16'bz;  // Controlled_Buffer controlled_buffer_7
  assign controlled_buffer_2_out = YO ? YReg_q : 16'bz;  // Controlled_Buffer controlled_buffer_8
  assign controlled_buffer_9_out = ZE ? controlled_buffer_2_out : 16'bz;  // Controlled_Buffer controlled_buffer_9
  assign controlled_buffer_2_out = ZO ? ZReg_q : 16'bz;  // Controlled_Buffer controlled_buffer_10
  assign controlled_buffer_11_out = IRE ? controlled_buffer_2_out : 16'bz;  // Controlled_Buffer controlled_buffer_11
  assign {controlled_buffer_12_out, controlled_buffer_2_out[10:0]} = IRO ? {InstructionRegister_q_2, InstructionRegister_q} : 16'bz;  // Controlled_Buffer controlled_buffer_12
  assign controlled_buffer_13_out = MAE ? controlled_buffer_2_out[10:0] : 11'bz;  // Controlled_Buffer controlled_buffer_13
  assign controlled_buffer_14_out = RAE ? controlled_buffer_2_out : 16'bz;  // Controlled_Buffer controlled_buffer_14
  assign controlled_buffer_2_out = RAO ? ram_1_dout : 16'bz;  // Controlled_Buffer controlled_buffer_15
  Pull_Resistor pull_resistor_15 (.node(controlled_buffer_2_out[1]));
  Pull_Resistor pull_resistor_16 (.node(controlled_buffer_2_out[0]));
  Register FlagsReg (.D(controlled_buffer_4_out), .en(FE), .clk(and_1_out), .Q(FlagsReg_q));  // open: clr
  Register #(.width(16)) XReg (.D(controlled_buffer_5_out), .en(XE), .clk(and_1_out), .Q(XReg_q));  // open: clr
  Register #(.width(16)) YReg (.D(controlled_buffer_7_out), .en(YE), .clk(and_1_out), .Q(YReg_q));  // open: clr
  Register #(.width(16)) ZReg (.D(controlled_buffer_9_out), .en(ZE), .clk(and_1_out), .Q(ZReg_q));  // open: clr
  Register #(.width(16)) InstructionRegister (
    .D(controlled_buffer_11_out), .en(IRE), .clk(and_1_out),
    .Q({InstructionRegister_q_2, InstructionRegister_q}));  // open: clr
  Register #(.width(11)) MemoryAddressRegister (
    .D(controlled_buffer_13_out), .en(MAE), .clk(and_1_out), .Q(MemoryAddressRegister_q));  // open: clr
  RAM #(.addrWidth(11), .dataWidth(16), .enables("line"), .\type ("nonvolatile")) ram_1 (
    .addr(MemoryAddressRegister_q), .we(RAE), .clk(and_1_out), .din(controlled_buffer_14_out),
    .dout(ram_1_dout));

  // Notes on the sheet:
  //   contents of rom_1 (hex, n*v repeats v):
  //   20080 40220 6*0 20080 40220 180 8021 4*0 20080 40220 180 2021 4*0 20080 40220 180 821 4*0 20080
  //   40220 8101 5*0 20080 40220 2101 5*0 20080 40220 901 5*0 20080 40220 180 2020 819 0 0 0 20080 40220
  //   180 2020 81d 0 0 0 20080 40220 6*0 20080 40220 8101 801b 4*0 20080 40220 180 201b 4*0 20080 40220
  //   180 81b 4*0 20080 40220 6*0 20080 40220 6*0 20080 40220 6*0 20080 40220 6*0 20080 40220 6*0 20080
  //   40220 6*0 20080 40220 6*0 20080 40220 6*0 20080 40220 6*0 20080 40220 6*0 20080 40220 6*0 20080
  //   40220 6*0 20080 40220 6*0 20080 40220 6*0 20080 40220 6*0 20080 40220 6*0 20080 40220 6*0 20080
  //   40220 6*0 20080 40220 6*0 20080 40220 6*0 20080 40220 180 8021 4*0 20080 40220 180 2021 4*0 20080
  //   40220 180 821 4*0 20080 40220 8101 5*0 20080 40220 2101 5*0 20080 40220 901 5*0 20080 40220 180 2020
  //   819 0 0 0 20080 40220 180 2020 81d 0 0 0 20080 40220 6*0 20080 40220 8101 801b 4*0 20080 40220 180
  //   201b 4*0 20080 40220 180 81b 4*0 20080 40220 6*0 20080 40220 6*0 20080 40220 6*0 20080 40220 6*0
  //   20080 40220 6*0 20080 40220 6*0 20080 40220 6*0 20080 40220 6*0 20080 40220 6*0 20080 40220 6*0
  //   20080 40220 6*0 20080 40220 6*0 20080 40220 6*0 20080 40220 6*0 20080 40220 6*0 20080 40220 6*0
  //   20080 40220 6*0 20080 40220 6*0 20080 40220 6*0 20080 40220 6*0 20080 40220 180 8021 4*0 20080 40220
  //   180 2021 4*0 20080 40220 180 821 4*0 20080 40220 8101 5*0 20080 40220 2101 5*0 20080 40220 901 5*0
  //   20080 40220 180 2020 819 0 0 0 20080 40220 180 2020 81d 0 0 0 20080 40220 6*0 20080 40220 8101 801b
  //   4*0 20080 40220 180 201b 4*0 20080 40220 180 81b 4*0 20080 40220 6*0 20080 40220 6*0 20080 40220 6*0
  //   20080 40220 6*0 20080 40220 6*0 20080 40220 6*0 20080 40220 6*0 20080 40220 6*0 20080 40220 6*0
  //   20080 40220 6*0 20080 40220 6*0 20080 40220 6*0 20080 40220 6*0 20080 40220 6*0 20080 40220 6*0
  //   20080 40220 6*0 20080 40220 6*0 20080 40220 6*0 20080 40220 6*0 20080 40220 6*0 20080 40220 180 8021
  //   4*0 20080 40220 180 2021 4*0 20080 40220 180 821 4*0 20080 40220 8101 5*0 20080 40220 2101 5*0 20080
  //   40220 901 5*0 20080 40220 180 2020 819 0 0 0 20080 40220 180 2020 81d 0 0 0 20080 40220 6*0 20080
  //   40220 8101 801b 4*0 20080 40220 180 201b 4*0 20080 40220 180 81b 4*0 20080 40220 6*0 20080 40220 6*0
  //   20080 40220 6*0 20080 40220 6*0 20080 40220 6*0 20080 40220 6*0 20080 40220 6*0 20080 40220 6*0
  //   20080 40220 6*0 20080 40220 6*0 20080 40220 6*0 20080 40220 6*0 20080 40220 6*0 20080 40220 6*0
  //   20080 40220 6*0 20080 40220 6*0 20080 40220 6*0 20080 40220 6*0 20080 40220 6*0 20080 40220 6*0
  //   20080 40220 180 8021 4*0 20080 40220 180 2021 4*0 20080 40220 180 821 4*0 20080 40220 8101 5*0 20080
  //   40220 2101 5*0 20080 40220 901 5*0 20080 40220 180 2020 819 0 0 0 20080 40220 180 2020 81d 0 0 0
  //   20080 40220 6*0 20080 40220 8101 801b 4*0 20080 40220 180 201b 4*0 20080 40220 180 81b 4*0 20080
  //   40220 6*0 20080 40220 6*0 20080 40220 6*0 20080 40220 6*0 20080 40220 6*0 20080 40220 6*0 20080
  //   40220 6*0 20080 40220 6*0 20080 40220 6*0 20080 40220 6*0 20080 40220 6*0 20080 40220 6*0 20080
  //   40220 6*0 20080 40220 6*0 20080 40220 6*0 20080 40220 6*0 20080 40220 6*0 20080 40220 6*0 20080
  //   40220 6*0 20080 40220 6*0 20080 40220 180 8021 4*0 20080 40220 180 2021 4*0 20080 40220 180 821 4*0
  //   20080 40220 8101 5*0 20080 40220 2101 5*0 20080 40220 901 5*0 20080 40220 180 2020 819 0 0 0 20080
  //   40220 180 2020 81d 0 0 0 20080 40220 6*0 20080 40220 8101 801b 4*0 20080 40220 180 201b 4*0 20080
  //   40220 180 81b 4*0 20080 40220 6*0 20080 40220 6*0 20080 40220 6*0 20080 40220 6*0 20080 40220 6*0
  //   20080 40220 6*0 20080 40220 6*0 20080 40220 6*0 20080 40220 6*0 20080 40220 6*0 20080 40220 6*0
  //   20080 40220 6*0 20080 40220 6*0 20080 40220 6*0 20080 40220 6*0 20080 40220 6*0 20080 40220 6*0
  //   20080 40220 6*0 20080 40220 6*0 20080 40220 6*0 20080 40220 180 8021 4*0 20080 40220 180 2021 4*0
  //   20080 40220 180 821 4*0 20080 40220 8101 5*0 20080 40220 2101 5*0 20080 40220 901 5*0 20080 40220
  //   180 2020 819 0 0 0 20080 40220 180 2020 81d 0 0 0 20080 40220 6*0 20080 40220 8101 801b 4*0 20080
  //   40220 180 201b 4*0 20080 40220 180 81b 4*0 20080 40220 6*0 20080 40220 6*0 20080 402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
endmodule

module ALU (
  input  [15:0] XReg,
  input  [15:0] YReg,
  input  ALS,
  input  ALC,
  output [15:0] ALUOut,
  output CFOut
);

  wire not_1_out;
  wire [15:0] controlled_buffer_1_out, xorregister_1_outreg;

  assign controlled_buffer_1_out = ALC ? 16'h1 : 16'bz;  // Controlled_Buffer controlled_buffer_1
  not not_1 (not_1_out, ALC);
  assign controlled_buffer_1_out = not_1_out ? YReg : 16'bz;  // Controlled_Buffer controlled_buffer_2
  FullAdder16Bit fulladder16bit_1 (.CI(ALS), .A(XReg), .B(xorregister_1_outreg), .S(ALUOut), .CO(CFOut));
  XORRegister xorregister_1 (.InReg(controlled_buffer_1_out), .CE(ALS), .OutReg(xorregister_1_outreg));
endmodule

module HalfAdder (
  input  A,
  input  B,
  output CO,
  output S
);

  and and_1 (CO, A, B);
  xor xor_1 (S, A, B);
endmodule

module FullAdder (
  input  CI,
  input  A,
  input  B,
  output S,
  output CO
);

  wire halfadder_1_co, halfadder_2_co, halfadder_2_s;

  HalfAdder halfadder_1 (.A(CI), .B(halfadder_2_s), .CO(halfadder_1_co), .S(S));
  HalfAdder halfadder_2 (.A(A), .B(B), .CO(halfadder_2_co), .S(halfadder_2_s));
  or or_1 (CO, halfadder_1_co, halfadder_2_co);
endmodule

module FullAdder4Bit (
  input  CI,
  input  [3:0] A,
  input  [3:0] B,
  output [3:0] S,
  output CO
);

  wire fulladder_1_co, fulladder_2_co, fulladder_3_co;

  FullAdder fulladder_1 (.CI(CI), .A(A[0]), .B(B[0]), .S(S[0]), .CO(fulladder_1_co));
  FullAdder fulladder_2 (.CI(fulladder_1_co), .A(A[1]), .B(B[1]), .S(S[1]), .CO(fulladder_2_co));
  FullAdder fulladder_3 (.CI(fulladder_2_co), .A(A[2]), .B(B[2]), .S(S[2]), .CO(fulladder_3_co));
  FullAdder fulladder_4 (.CI(fulladder_3_co), .A(A[3]), .B(B[3]), .S(S[3]), .CO(CO));
endmodule

module FullAdder8Bit (
  input  CI,
  input  [7:0] A,
  input  [7:0] B,
  output [7:0] S,
  output CO
);

  wire fulladder4bit_1_co;

  FullAdder4Bit fulladder4bit_1 (.CI(CI), .A(A[3:0]), .B(B[3:0]), .S(S[3:0]), .CO(fulladder4bit_1_co));
  FullAdder4Bit fulladder4bit_2 (.CI(fulladder4bit_1_co), .A(A[7:4]), .B(B[7:4]), .S(S[7:4]), .CO(CO));
endmodule

module FullAdder16Bit (
  input  CI,
  input  [15:0] A,
  input  [15:0] B,
  output [15:0] S,
  output CO
);

  wire fulladder8bit_1_co;

  FullAdder8Bit fulladder8bit_1 (.CI(CI), .A(A[7:0]), .B(B[7:0]), .S(S[7:0]), .CO(fulladder8bit_1_co));
  FullAdder8Bit fulladder8bit_2 (.CI(fulladder8bit_1_co), .A(A[15:8]), .B(B[15:8]), .S(S[15:8]), .CO(CO));
endmodule

module XORRegister (
  input  [15:0] InReg,
  input  CE,
  output [15:0] OutReg
);

  xor xor_1 (OutReg[0], InReg[0], CE);
  xor xor_2 (OutReg[1], InReg[1], CE);
  xor xor_3 (OutReg[2], InReg[2], CE);
  xor xor_4 (OutReg[3], InReg[3], CE);
  xor xor_5 (OutReg[4], InReg[4], CE);
  xor xor_6 (OutReg[5], InReg[5], CE);
  xor xor_7 (OutReg[6], InReg[6], CE);
  xor xor_8 (OutReg[7], InReg[7], CE);
  xor xor_9 (OutReg[8], InReg[8], CE);
  xor xor_10 (OutReg[9], InReg[9], CE);
  xor xor_11 (OutReg[10], InReg[10], CE);
  xor xor_12 (OutReg[11], InReg[11], CE);
  xor xor_13 (OutReg[12], InReg[12], CE);
  xor xor_14 (OutReg[13], InReg[13], CE);
  xor xor_15 (OutReg[14], InReg[14], CE);
  xor xor_16 (OutReg[15], InReg[15], CE);
endmodule
